# Fritzing sketch 1-wire-to-serial-pcb-2.74x4.73cm (saved by Fritzing 0.7.7b)
breadboards: 1

parts:
  DS18S20 = mystery part, 3 pins [chip_label=? spacing=300mil]
  D2 = Rectifier Diode [part_number=1N4001 package="300 mil [THT]"]
  D3 = Rectifier Diode [part_number=1N4001 package="300 mil [THT]"]
  D1 = Rectifier Diode [part_number=1N4001 package="300 mil [THT]"]
  UART = Barometric Pressure Sensor
  D4 = Rectifier Diode [part_number=1N4001 package="300 mil [THT]"]
  R1 = Resistor [tolerance=±5% resistance=220 package=THT]

nets:
  N1: DS18S20.pin1, DS18S20.pin3, D2.anode, D3.anode, UART.MISO, D4.cathode, R1.Pin_0
  N2: DS18S20.pin2, D2.cathode, D3.cathode, D1.cathode, D1.anode, UART.DRDY, UART.CSB
  N3: UART.MOSI, D4.anode, R1.Pin_1

notes:
  dtr
  gnd
  rxd
  txd
  klenov v.
  1
  temp sensor
  parasitic mode
  D2
  D3
  D4
  D1
  R1
